# Fritzing sketch traethlin (saved by Fritzing 0.9.6b)

parts:
  part = Raspberry Pi 4B
  A1 = ESP32 Wroom 32E dev board
  Steering = Basic Servo
  Front_diff = Basic Servo
  Rear_diff = Basic Servo
  Power = Dagu DGServo 9g header connector (female) [package=THT]
  DC1 = DC_DC_XL4016 [package=board_screw]
  Gearbox = Basic Servo
  5V = Screw terminal - 2 pins [package=THT]
  3_3V = Screw terminal - 2 pins [package=THT]
  GND = Screw terminal - 2 pins [package=THT]

nets:
  N1: part.3V3, A1.Pin_1, 3_3V.pin1, 3_3V.pin2
  N2: part.5V, DC1.OUT+, 5V.pin1, 5V.pin2
  N3: part.GND, A1.Pin_32, A1.Pin_38, DC1.OUT-, GND.pin1, GND.pin2
  VCC: Steering.vcc, Front_diff.vcc, Rear_diff.vcc, Power.Vcc, DC1.IN+, Gearbox.vcc
  GND: Rear_diff.gnd, Power.gnd, DC1.IN-, Gearbox.gnd

custom parts:
  ESP32 Wroom 32E dev board: The ESP32 WROOM-32E is a versatile and powerful module built around Espressif’s ESP32 chipset. It offers dual-core processing, integrated Wi-Fi and Bluetooth connectivity, and boasts a wide range of peripheral interfaces.
